// Logisim project lab08part3-ded57.circ as structural Verilog: 1 circuit, main circuit main
module main (
  input  A,
  input  B,
  input  C,
  output V
);

  wire A_prime_B_prime_out, A_prime_C_prime_out, B_prime_C_prime_out, not_1_out, not_2_out, not_3_out;

  not not_1 (not_1_out, A);
  not not_2 (not_2_out, B);
  not not_3 (not_3_out, C);
  and A_prime_B_prime (A_prime_B_prime_out, not_1_out, not_2_out);
  and A_prime_C_prime (A_prime_C_prime_out, not_1_out, not_3_out);
  and B_prime_C_prime (B_prime_C_prime_out, not_2_out, not_3_out);
  or or_1 (V, A_prime_B_prime_out, A_prime_C_prime_out, B_prime_C_prime_out);
endmodule
