// Logisim project lab09part2-ded57.circ as structural Verilog: 2 circuits, main circuit main
module main (
);

  wire Batch_1_out, Batch_2_out, Batch_3_out, Batch_4_out, Batch_5_out, Batch_6_out, clock_1_out,
       cookiewatcher_1_cookiesburnt, cookiewatcher_1_cookiesdone, cookiewatcher_2_cookiesburnt,
       cookiewatcher_2_cookiesdone, cookiewatcher_3_cookiesburnt, cookiewatcher_3_cookiesdone,
       cookiewatcher_4_cookiesburnt, cookiewatcher_4_cookiesdone, cookiewatcher_5_cookiesburnt,
       cookiewatcher_5_cookiesdone, cookiewatcher_6_cookiesburnt, cookiewatcher_6_cookiesdone;

  Clock clock_1 (.out(clock_1_out));
  Button Batch_1 (.out(Batch_1_out));
  Button Batch_2 (.out(Batch_2_out));
  Button Batch_3 (.out(Batch_3_out));
  Button Batch_4 (.out(Batch_4_out));
  Button Batch_5 (.out(Batch_5_out));
  Button Batch_6 (.out(Batch_6_out));
  CookieWatcher cookiewatcher_1 (
    .Clock(clock_1_out), .BatchHandled(Batch_1_out), .CookiesBurnt(cookiewatcher_1_cookiesburnt),
    .CookiesDone(cookiewatcher_1_cookiesdone));
  CookieWatcher cookiewatcher_2 (
    .Clock(clock_1_out), .BatchHandled(Batch_2_out), .CookiesBurnt(cookiewatcher_2_cookiesburnt),
    .CookiesDone(cookiewatcher_2_cookiesdone));
  CookieWatcher cookiewatcher_3 (
    .Clock(clock_1_out), .BatchHandled(Batch_3_out), .CookiesBurnt(cookiewatcher_3_cookiesburnt),
    .CookiesDone(cookiewatcher_3_cookiesdone));
  CookieWatcher cookiewatcher_4 (
    .Clock(clock_1_out), .BatchHandled(Batch_4_out), .CookiesBurnt(cookiewatcher_4_cookiesburnt),
    .CookiesDone(cookiewatcher_4_cookiesdone));
  CookieWatcher cookiewatcher_5 (
    .Clock(clock_1_out), .BatchHandled(Batch_5_out), .CookiesBurnt(cookiewatcher_5_cookiesburnt),
    .CookiesDone(cookiewatcher_5_cookiesdone));
  CookieWatcher cookiewatcher_6 (
    .Clock(clock_1_out), .BatchHandled(Batch_6_out), .CookiesBurnt(cookiewatcher_6_cookiesburnt),
    .CookiesDone(cookiewatcher_6_cookiesdone));
  LED led_1 (.in(cookiewatcher_1_cookiesburnt));
  LED led_2 (.in(cookiewatcher_1_cookiesdone));
  LED led_3 (.in(cookiewatcher_2_cookiesburnt));
  LED led_4 (.in(cookiewatcher_2_cookiesdone));
  LED led_5 (.in(cookiewatcher_3_cookiesburnt));
  LED led_6 (.in(cookiewatcher_3_cookiesdone));
  LED led_7 (.in(cookiewatcher_4_cookiesburnt));
  LED led_8 (.in(cookiewatcher_4_cookiesdone));
  LED led_9 (.in(cookiewatcher_5_cookiesburnt));
  LED led_10 (.in(cookiewatcher_5_cookiesdone));
  LED led_11 (.in(cookiewatcher_6_cookiesburnt));
  LED led_12 (.in(cookiewatcher_6_cookiesdone));
endmodule

module CookieWatcher (
  input  Clock,
  input  BatchHandled,
  output CookiesBurnt,
  output CookiesDone
);

  wire [8:0] counter_1_q;

  Counter #(.width(10), .max('h3ff), .ongoal("stay")) counter_1 (
    .load(1'b0), .count(1'b1), .Q({CookiesDone, counter_1_q}), .clk(Clock), .clr(BatchHandled));  // open: D, carry
  and and_1 (CookiesBurnt, counter_1_q[8], CookiesDone);
endmodule
