// Logisim project lab10part2-ded57.circ as structural Verilog: 1 circuit, main circuit main
module main (
  input  [3:0] in_1,
  input  [3:0] in_2,
  output [3:0] out_3
);

  wire button_1_out, clock_1_out, not_1_out, undriven;
  wire [3:0] ram_1_data, register_1_q;

  assign out_3 = undriven ? in_1 : 4'bz;  // Controlled_Buffer controlled_buffer_1
  not not_1 (not_1_out, undriven);
  Register #(.width(4)) register_1 (.D(in_2), .Q(register_1_q), .clk(clock_1_out));  // open: en, clr
  Clock clock_1 (.out(clock_1_out));
  RAM #(.addrWidth(4), .dataWidth(4)) ram_1 (
    .addr(register_1_q), .data(ram_1_data), .clk(clock_1_out), .ld(not_1_out), .clr(button_1_out));  // open: sel
  Controlled_Buffer #(.width(4)) controlled_buffer_2 (.in(out_3), .out(ram_1_data));  // open: en
  Button button_1 (.out(button_1_out));
  Register #(.width(4)) register_2 (.Q(out_3), .clk(clock_1_out));  // open: D, en, clr
endmodule
