// Logisim project lab11partC-ded57.circ as structural Verilog: 3 circuits, main circuit main
module main (
);

  wire clock_1_out, outputtable_1_out, shift_register_1_out;
  wire [1:0] nextstate_1_out_0, register_1_q;

  Shift_Register shift_register_1 (
    .clk(clock_1_out), .out(shift_register_1_out));  // open: shift, in, load, clr, d0, q0, d1, q1, d2, q2, d3, q3, d4, q4, d5, q5, d6, q6, d7, q7
  Register #(.width(2)) register_1 (.D(nextstate_1_out_0), .Q(register_1_q), .clk(clock_1_out));  // open: en, clr
  Clock clock_1 (.out(clock_1_out));
  NextState nextstate_1 (
    .State_0(register_1_q[0]), .State_1(register_1_q[1]), .State_Hears(shift_register_1_out),
    .Out_0(nextstate_1_out_0[0]), .Out_1(nextstate_1_out_0[1]));
  OutputTable outputtable_1 (.State_0(register_1_q[0]), .State_1(register_1_q[1]), .Out(outputtable_1_out));
  LED led_1 (.in(outputtable_1_out));
endmodule

// Output
module OutputTable (
  input  State_0,
  input  State_1,
  output Out
);

  and and_1 (Out, State_0, State_1);
endmodule

// Next-state
module NextState (
  input  State_0,
  input  State_1,
  input  State_Hears,
  output Out_0,
  output Out_1
);

  wire and_1_out, and_2_out, and_3_out, and_4_out, not_1_out, not_2_out, not_3_out, not_4_out, not_5_out;

  not not_1 (not_1_out, State_0);
  not not_2 (not_2_out, State_1);
  not not_3 (not_3_out, State_Hears);
  not not_4 (not_4_out, State_1);
  not not_5 (not_5_out, State_1);
  and and_1 (and_1_out, not_1_out, State_1, State_Hears);
  and and_2 (and_2_out, State_0, not_2_out, not_3_out);
  and and_3 (and_3_out, not_4_out, State_Hears);
  and and_4 (and_4_out, State_0, not_5_out);
  or or_1 (Out_0, and_1_out, and_2_out);
  or or_2 (Out_1, and_3_out, and_4_out);
endmodule
