// Logisim project lab12-ded57.circ as structural Verilog: 3 circuits, main circuit main
module main (
  input  [15:0] temp_instruction
);

  wire adder_1_cout, clock_1_out, controlled_inverter_1_out, Select;
  wire [1:0] ALUOp;
  wire [7:0] A_q, adder_1_out, B_q, register_1_q, undriven, undriven_2;

  Adder adder_1 (.a(8'h1), .b(register_1_q), .out(adder_1_out), .cin(1'b0), .cout(adder_1_cout));
  Register register_1 (.D(adder_1_out), .Q(register_1_q), .clk(clock_1_out));  // open: en, clr
  Clock clock_1 (.out(clock_1_out));
  ROM #(.dataWidth(16)) rom_1 (.addr(register_1_q), .sel(clock_1_out));  // open: data
  Control control_1 (
    .Op3(temp_instruction[15]), .Op2(temp_instruction[14]), .Op1(temp_instruction[13]),
    .Op0(temp_instruction[12]), .ALUOp1(ALUOp[1]), .ALUOp0(ALUOp[0]), .Select(Select));
  Register A (.D(undriven), .en(controlled_inverter_1_out), .Q(A_q), .clk(clock_1_out));  // open: clr
  Controlled_Inverter controlled_inverter_1 (.in(temp_instruction[11]), .out(controlled_inverter_1_out));  // open: en
  Register B (.D(undriven_2), .en(temp_instruction[11]), .Q(B_q), .clk(clock_1_out));  // open: clr
  ALU alu_1 (.A(A_q), .B(B_q), .ALUOp(ALUOp));  // open: out_4
  Multiplexer #(.width(8)) multiplexer_1 (
    .in0(undriven), .in1(undriven_2), .out(temp_instruction[7:0]));  // open: sel, en
  // also tied to VCC on the sheet: clock_1_out
endmodule

module ALU (
  input  [7:0] A,
  input  [7:0] B,
  input  [1:0] ALUOp,
  output [7:0] out_4
);

  wire [7:0] adder_1_out, and_1_out, or_1_out, subtractor_1_out;

  Adder adder_1 (.a(A), .b(B), .out(adder_1_out), .cin(1'b0));  // open: cout
  Subtractor subtractor_1 (.a(A), .b(B), .out(subtractor_1_out), .bin(1'b0));  // open: bout
  assign or_1_out = A | B;  // OR_Gate or_1, 8 bits wide
  assign and_1_out = A & B;  // AND_Gate and_1, 8 bits wide
  Multiplexer #(.select(2), .width(8), .enable("false")) multiplexer_1 (
    .in0(adder_1_out), .in1(subtractor_1_out), .in2(or_1_out), .in3(and_1_out), .out(out_4), .sel(ALUOp));
endmodule

module Control (
  input  Op3,
  input  Op2,
  input  Op1,
  input  Op0,
  output ALUOp1,
  output ALUOp0,
  output Select
);

  wire not_2_out, not_3_out;

  not not_1 (ALUOp1, Op1);
  not not_2 (not_2_out, Op2);
  and and_1 (Select, not_2_out, not_3_out);
  not not_3 (not_3_out, Op1);

  assign ALUOp0 = Op0;
endmodule
